// Logisim project trafficLight.circ as structural Verilog: 9 circuits, main circuit main
module main (
);

  wire and_1_out, and_2_out, CLK, d_ff_1_q, d_ff_1_qn, nor_1_out, or_1_out, or_2_out, roj, ver;
  wire [3:0] vrd_c;
  wire [4:0] roj_c;
  wire [6:0] DDR, DDV, DUR, DUV;

  and and_1 (and_1_out, ver, CLK);
  and and_2 (and_2_out, roj, CLK);
  counter_12SEGUNDOS _12_Seg (.CLOCK(and_1_out), .Q3(vrd_c[3]), .Q2(vrd_c[2]), .Q1(vrd_c[1]), .Q0(vrd_c[0]));
  counter_24SEGUNDOS _24_Seg (
    .CLOCK(and_2_out), .Q4(roj_c[4]), .Q3(roj_c[3]), .Q2(roj_c[2]), .Q1(roj_c[1]), .Q0(roj_c[0]));
  DECODIFICADORES_decenas DEC_DECENAS (
    .A4(1'b0), .A3(vrd_c[3]), .A2(vrd_c[2]), .A1(vrd_c[1]), .A0(vrd_c[0]), .A(DDV[0]), .B(DDV[1]),
    .C(DDV[2]), .D(DDV[3]), .E(DDV[4]), .F(DDV[5]), .G(DDV[6]));
  DECODIFICADORES_decenas DEC_DECENAS_2 (
    .A4(roj_c[4]), .A3(roj_c[3]), .A2(roj_c[2]), .A1(roj_c[1]), .A0(roj_c[0]), .A(DDR[0]), .B(DDR[1]),
    .C(DDR[2]), .D(DDR[3]), .E(DDR[4]), .F(DDR[5]), .G(DDR[6]));
  or or_1 (or_1_out, vrd_c[3], vrd_c[2], vrd_c[1], vrd_c[0]);
  or or_2 (or_2_out, roj_c[4], roj_c[3], roj_c[2], roj_c[1], roj_c[0]);
  nor nor_1 (nor_1_out, vrd_c[3], vrd_c[2], vrd_c[1], vrd_c[0], roj_c[4], roj_c[3], roj_c[2], roj_c[1], roj_c[0]);
  D_Flip_Flop d_ff_1 (.clk(nor_1_out), .D(d_ff_1_qn), .Q(d_ff_1_q), .Qn(d_ff_1_qn));  // open: preset, en, reset
  DECODIFICADOR_unidades DEC_UNIDADES (
    .A4(1'b0), .A3(vrd_c[3]), .A2(vrd_c[2]), .A1(vrd_c[1]), .A0(vrd_c[0]), .A(DUV[0]), .B(DUV[1]),
    .C(DUV[2]), .D(DUV[3]), .E(DUV[4]), .F(DUV[5]), .G(DUV[6]));
  DECODIFICADOR_unidades DEC_UNIDADES_2 (
    .A4(roj_c[4]), .A3(roj_c[3]), .A2(roj_c[2]), .A1(roj_c[1]), .A0(roj_c[0]), .A(DUR[0]), .B(DUR[1]),
    .C(DUR[2]), .D(DUR[3]), .E(DUR[4]), .F(DUR[5]), .G(DUR[6]));
  or or_3 (ver, or_1_out, d_ff_1_qn);
  or or_4 (roj, or_2_out, d_ff_1_q);
  Clock clock_1 (.out(CLK));
  _7_Segment_Display u_7_segment_display_1 (
    .g(DDV[6]), .f(DDV[5]), .a(DDV[0]), .b(DDV[1]), .e(DDV[4]), .d(DDV[3]), .c(DDV[2]), .dp(1'b0));
  _7_Segment_Display u_7_segment_display_2 (
    .g(DDR[6]), .f(DDR[5]), .a(DDR[0]), .b(DDR[1]), .e(DDR[4]), .d(DDR[3]), .c(DDR[2]), .dp(1'b0));
  LED Verde (.in(ver));
  LED Rojo (.in(roj));
  _7_Segment_Display u_7_segment_display_3 (
    .g(DUV[6]), .f(DUV[5]), .a(DUV[0]), .b(DUV[1]), .e(DUV[4]), .d(DUV[3]), .c(DUV[2]), .dp(1'b0));
  _7_Segment_Display u_7_segment_display_4 (
    .g(DUR[6]), .f(DUR[5]), .a(DUR[0]), .b(DUR[1]), .e(DUR[4]), .d(DUR[3]), .c(DUR[2]), .dp(1'b0));
endmodule

module counter_12SEGUNDOS (
  input  CLOCK,
  output Q3,
  output Q2,
  output Q1,
  output Q0
);

  wire comb12_1_qa0, comb12_1_qa1, comb12_1_qa2, comb12_1_qa3;

  flip_flop_4_bit_TIPO_D flip_flop_4_bit_tipo_d_1 (
    .in_1(CLOCK), .D3(comb12_1_qa3), .D2(comb12_1_qa2), .D1(comb12_1_qa1), .D0(comb12_1_qa0), .Q3(Q3),
    .Q2(Q2), .Q1(Q1), .Q0(Q0));
  COMB12 comb12_1 (
    .Q3(Q3), .Q2(Q2), .Q1(Q1), .Q0(Q0), .QA3(comb12_1_qa3), .QA2(comb12_1_qa2), .QA1(comb12_1_qa1),
    .QA0(comb12_1_qa0));
endmodule

module flip_flop_4_bit_TIPO_D (
  input  in_1,
  input  D3,
  input  D2,
  input  D1,
  input  D0,
  output Q3,
  output Q2,
  output Q1,
  output Q0
);

  D_Flip_Flop d_ff_1 (.clk(in_1), .D(D3), .Q(Q3));  // open: Qn, preset, en, reset
  D_Flip_Flop d_ff_2 (.clk(in_1), .D(D2), .Q(Q2));  // open: Qn, preset, en, reset
  D_Flip_Flop d_ff_3 (.clk(in_1), .D(D1), .Q(Q1));  // open: Qn, preset, en, reset
  D_Flip_Flop d_ff_4 (.clk(in_1), .D(D0), .Q(Q0));  // open: Qn, preset, en, reset
endmodule

module COMB12 (
  input  Q3,
  input  Q2,
  input  Q1,
  input  Q0,
  output QA3,
  output QA2,
  output QA1,
  output QA0
);

  wire and_1_out, and_2_out, and_3_out, and_4_out, and_5_out, and_6_out, and_7_out, and_8_out, and_9_out,
       and_10_out, and_11_out, and_12_out, and_13_out, and_14_out, not_1_out, not_2_out, not_3_out,
       not_4_out, not_5_out, not_6_out, not_7_out, not_8_out, not_9_out, not_10_out, not_11_out, not_12_out,
       not_13_out, not_14_out, not_15_out, not_16_out, not_17_out;

  not not_1 (not_1_out, Q3);
  not not_2 (not_2_out, Q2);
  not not_3 (not_3_out, Q1);
  not not_4 (not_4_out, Q0);
  not not_5 (not_5_out, Q2);
  not not_6 (not_6_out, Q2);
  not not_7 (not_7_out, Q0);
  not not_8 (not_8_out, Q2);
  not not_9 (not_9_out, Q1);
  and and_1 (and_1_out, not_8_out, not_9_out, not_10_out);
  not not_10 (not_10_out, Q0);
  and and_2 (and_2_out, Q2, Q0);
  and and_3 (and_3_out, Q2, Q1);
  and and_4 (and_4_out, Q1, Q0);
  and and_5 (and_5_out, Q2, not_11_out, not_12_out);
  not not_11 (not_11_out, Q1);
  not not_12 (not_12_out, Q0);
  and and_6 (and_6_out, Q3, not_13_out, not_14_out);
  not not_13 (not_13_out, Q1);
  not not_14 (not_14_out, Q0);
  and and_7 (and_7_out, Q1, not_15_out);
  not not_15 (not_15_out, Q0);
  and and_8 (and_8_out, Q2, not_16_out);
  not not_16 (not_16_out, Q0);
  and and_9 (and_9_out, Q3, not_17_out);
  not not_17 (not_17_out, Q0);
  and and_10 (and_10_out, Q3, Q2);
  and and_11 (and_11_out, not_1_out, not_2_out, not_3_out, not_4_out);
  and and_12 (and_12_out, Q3, not_5_out, Q0);
  and and_13 (and_13_out, Q3, not_6_out, Q1);
  and and_14 (and_14_out, Q3, Q2, not_7_out);
  or or_1 (QA2, and_1_out, and_2_out, and_3_out);
  or or_2 (QA1, and_4_out, and_5_out, and_6_out);
  or or_3 (QA0, and_7_out, and_8_out, and_9_out, and_10_out);
  or or_4 (QA3, and_11_out, and_12_out, and_13_out, and_14_out);
endmodule

module counter_24SEGUNDOS (
  input  CLOCK,
  output Q4,
  output Q3,
  output Q2,
  output Q1,
  output Q0
);

  wire comb24_1_qa0, comb24_1_qa1, comb24_1_qa2, comb24_1_qa3, comb24_1_qa4;

  flip_flop_5_bit_TIPO_D flip_flop_5_bit_tipo_d_1 (
    .CLOCK(CLOCK), .D4(comb24_1_qa4), .D3(comb24_1_qa3), .D2(comb24_1_qa2), .D1(comb24_1_qa1),
    .D0(comb24_1_qa0), .Q4(Q4), .Q3(Q3), .Q2(Q2), .Q1(Q1), .Q0(Q0));
  COMB24 comb24_1 (
    .Q4(Q4), .Q3(Q3), .Q2(Q2), .Q1(Q1), .Q0(Q0), .QA4(comb24_1_qa4), .QA3(comb24_1_qa3), .QA2(comb24_1_qa2),
    .QA1(comb24_1_qa1), .QA0(comb24_1_qa0));
endmodule

module flip_flop_5_bit_TIPO_D (
  input  CLOCK,
  input  D4,
  input  D3,
  input  D2,
  input  D1,
  input  D0,
  output Q4,
  output Q3,
  output Q2,
  output Q1,
  output Q0
);

  D_Flip_Flop d_ff_1 (.clk(CLOCK), .D(D4), .Q(Q4));  // open: Qn, preset, en, reset
  D_Flip_Flop d_ff_2 (.clk(CLOCK), .D(D3), .Q(Q3));  // open: Qn, preset, en, reset
  D_Flip_Flop d_ff_3 (.clk(CLOCK), .D(D2), .Q(Q2));  // open: Qn, preset, en, reset
  D_Flip_Flop d_ff_4 (.clk(CLOCK), .D(D1), .Q(Q1));  // open: Qn, preset, en, reset
  D_Flip_Flop d_ff_5 (.clk(CLOCK), .D(D0), .Q(Q0));  // open: Qn, preset, en, reset
endmodule

module COMB24 (
  input  Q4,
  input  Q3,
  input  Q2,
  input  Q1,
  input  Q0,
  output QA4,
  output QA3,
  output QA2,
  output QA1,
  output QA0
);

  wire and_1_out, and_2_out, and_3_out, and_4_out, and_5_out, and_6_out, and_7_out, and_8_out, and_9_out,
       and_10_out, and_11_out, and_12_out, and_13_out, and_14_out, and_15_out, and_16_out, and_17_out,
       and_18_out, and_19_out, and_20_out, and_21_out, not_1_out, not_2_out, not_3_out, not_4_out, not_5_out,
       not_6_out, not_7_out, not_8_out, not_9_out, not_10_out, not_11_out, not_12_out, not_13_out,
       not_14_out, not_15_out, not_16_out, not_17_out, not_18_out, not_19_out, not_20_out, not_21_out,
       not_22_out, not_23_out, not_24_out, not_25_out;

  not not_1 (not_1_out, Q4);
  not not_2 (not_2_out, Q3);
  not not_3 (not_3_out, Q2);
  not not_4 (not_4_out, Q1);
  not not_5 (not_5_out, Q0);
  not not_6 (not_6_out, Q3);
  not not_7 (not_7_out, Q2);
  not not_8 (not_8_out, Q1);
  not not_9 (not_9_out, Q0);
  not not_10 (not_10_out, Q2);
  not not_11 (not_11_out, Q1);
  not not_12 (not_12_out, Q0);
  not not_13 (not_13_out, Q2);
  not not_14 (not_14_out, Q1);
  not not_15 (not_15_out, Q0);
  not not_16 (not_16_out, Q1);
  not not_17 (not_17_out, Q0);
  not not_18 (not_18_out, Q1);
  not not_19 (not_19_out, Q0);
  not not_20 (not_20_out, Q1);
  not not_21 (not_21_out, Q0);
  not not_22 (not_22_out, Q0);
  not not_23 (not_23_out, Q0);
  not not_24 (not_24_out, Q0);
  not not_25 (not_25_out, Q0);
  and and_1 (and_1_out, not_1_out, not_2_out, not_3_out, not_4_out, not_5_out);
  and and_2 (and_2_out, Q4, Q0);
  and and_3 (and_3_out, Q4, Q1);
  and and_4 (and_4_out, Q4, Q2);
  and and_5 (and_5_out, Q4, Q3);
  and and_6 (and_6_out, not_6_out, not_7_out, not_8_out, not_9_out);
  and and_7 (and_7_out, Q3, Q0);
  and and_8 (and_8_out, Q3, Q1);
  and and_9 (and_9_out, Q3, Q2);
  and and_10 (and_10_out, Q2, Q0);
  and and_11 (and_11_out, Q2, Q1);
  and and_12 (and_12_out, Q3, not_10_out, not_11_out, not_12_out);
  and and_13 (and_13_out, Q4, not_13_out, not_14_out, not_15_out);
  and and_14 (and_14_out, Q1, Q0);
  and and_15 (and_15_out, Q2, not_16_out, not_17_out);
  and and_16 (and_16_out, Q3, not_18_out, not_19_out);
  and and_17 (and_17_out, Q4, not_20_out, not_21_out);
  and and_18 (and_18_out, Q1, not_22_out);
  and and_19 (and_19_out, Q2, not_23_out);
  and and_20 (and_20_out, Q3, not_24_out);
  and and_21 (and_21_out, Q4, not_25_out);
  or or_1 (QA4, and_1_out, and_2_out, and_3_out, and_4_out, and_5_out);
  or or_2 (QA3, and_6_out, and_7_out, and_8_out, and_9_out);
  or or_3 (QA2, and_10_out, and_11_out, and_12_out, and_13_out);
  or or_4 (QA1, and_14_out, and_15_out, and_16_out, and_17_out);
  or or_5 (QA0, and_18_out, and_19_out, and_20_out, and_21_out);
endmodule

module DECODIFICADOR_unidades (
  input  A4,
  input  A3,
  input  A2,
  input  A1,
  input  A0,
  output A,
  output B,
  output C,
  output D,
  output E,
  output F,
  output G
);

  wire and_1_out, and_2_out, and_3_out, and_4_out, and_5_out, and_6_out, and_7_out, and_8_out, and_9_out,
       and_10_out, and_11_out, and_12_out, and_13_out, and_14_out, and_15_out, and_16_out, and_17_out,
       and_18_out, and_19_out, and_20_out, and_21_out, and_22_out, and_23_out, and_24_out, and_25_out,
       and_26_out, and_27_out, and_28_out, and_29_out, and_30_out, and_31_out, and_32_out, and_33_out,
       and_34_out, and_35_out, and_36_out, and_37_out, and_38_out, and_39_out, and_40_out, and_41_out,
       and_42_out, and_43_out, and_44_out, and_45_out, and_46_out, and_47_out, and_48_out, and_49_out,
       and_50_out, and_51_out, and_52_out, and_53_out, and_54_out, and_55_out, and_56_out, and_57_out,
       not_1_out, not_2_out, not_3_out, not_4_out, not_5_out, not_6_out, not_7_out, not_8_out, not_9_out,
       not_10_out, not_11_out, not_12_out, not_13_out, not_14_out, not_15_out, not_16_out, not_17_out,
       not_18_out, not_19_out, not_20_out, not_21_out, not_22_out, not_23_out, not_24_out, not_25_out,
       not_26_out, not_27_out, not_28_out, not_29_out, not_30_out, not_31_out, not_32_out, not_33_out,
       not_34_out, not_35_out, not_36_out, not_37_out, not_38_out, not_39_out, not_40_out, not_41_out,
       not_42_out, not_43_out, not_44_out, not_45_out, not_46_out, not_47_out, not_48_out, not_49_out,
       not_50_out, not_51_out, not_52_out, not_53_out, not_54_out, not_55_out, not_56_out, not_57_out,
       not_58_out, not_59_out, not_60_out, not_61_out, not_62_out, not_63_out, not_64_out, not_65_out,
       not_66_out, not_67_out, not_68_out, not_69_out, not_70_out, not_71_out, not_72_out, not_73_out,
       not_74_out, not_75_out, not_76_out, not_77_out, not_78_out, not_79_out, not_80_out, not_81_out,
       not_82_out, not_83_out, not_84_out, not_85_out, not_86_out, not_87_out, not_88_out, not_89_out,
       not_90_out, not_91_out, not_92_out, not_93_out, not_94_out, not_95_out;

  not not_1 (not_1_out, A4);
  not not_2 (not_2_out, A2);
  not not_3 (not_3_out, A0);
  not not_4 (not_4_out, A3);
  not not_5 (not_5_out, A4);
  not not_6 (not_6_out, A1);
  not not_7 (not_7_out, A1);
  not not_8 (not_8_out, A3);
  not not_9 (not_9_out, A2);
  not not_10 (not_10_out, A3);
  not not_11 (not_11_out, A0);
  not not_12 (not_12_out, A4);
  not not_13 (not_13_out, A2);
  not not_14 (not_14_out, A4);
  not not_15 (not_15_out, A1);
  not not_16 (not_16_out, A0);
  not not_17 (not_17_out, A3);
  not not_18 (not_18_out, A2);
  not not_19 (not_19_out, A3);
  not not_20 (not_20_out, A2);
  not not_21 (not_21_out, A3);
  not not_22 (not_22_out, A2);
  not not_23 (not_23_out, A4);
  not not_24 (not_24_out, A1);
  not not_25 (not_25_out, A4);
  not not_26 (not_26_out, A0);
  not not_27 (not_27_out, A1);
  not not_28 (not_28_out, A0);
  not not_29 (not_29_out, A3);
  not not_30 (not_30_out, A1);
  not not_31 (not_31_out, A2);
  not not_32 (not_32_out, A1);
  not not_33 (not_33_out, A4);
  not not_34 (not_34_out, A3);
  not not_35 (not_35_out, A4);
  not not_36 (not_36_out, A3);
  not not_37 (not_37_out, A0);
  not not_38 (not_38_out, A2);
  not not_39 (not_39_out, A1);
  not not_40 (not_40_out, A4);
  not not_41 (not_41_out, A2);
  not not_42 (not_42_out, A0);
  not not_43 (not_43_out, A4);
  not not_44 (not_44_out, A3);
  not not_45 (not_45_out, A2);
  not not_46 (not_46_out, A3);
  not not_47 (not_47_out, A0);
  not not_48 (not_48_out, A2);
  not not_49 (not_49_out, A0);
  not not_50 (not_50_out, A4);
  not not_51 (not_51_out, A1);
  not not_52 (not_52_out, A1);
  not not_53 (not_53_out, A0);
  not not_54 (not_54_out, A4);
  not not_55 (not_55_out, A3);
  not not_56 (not_56_out, A0);
  not not_57 (not_57_out, A2);
  not not_58 (not_58_out, A1);
  not not_59 (not_59_out, A4);
  not not_60 (not_60_out, A2);
  not not_61 (not_61_out, A0);
  not not_62 (not_62_out, A3);
  not not_63 (not_63_out, A0);
  not not_64 (not_64_out, A2);
  not not_65 (not_65_out, A0);
  not not_66 (not_66_out, A1);
  not not_67 (not_67_out, A0);
  not not_68 (not_68_out, A3);
  not not_69 (not_69_out, A0);
  not not_70 (not_70_out, A3);
  not not_71 (not_71_out, A1);
  not not_72 (not_72_out, A0);
  not not_73 (not_73_out, A4);
  not not_74 (not_74_out, A3);
  not not_75 (not_75_out, A1);
  not not_76 (not_76_out, A4);
  not not_77 (not_77_out, A3);
  not not_78 (not_78_out, A0);
  not not_79 (not_79_out, A2);
  not not_80 (not_80_out, A1);
  not not_81 (not_81_out, A0);
  not not_82 (not_82_out, A4);
  not not_83 (not_83_out, A3);
  not not_84 (not_84_out, A2);
  not not_85 (not_85_out, A1);
  not not_86 (not_86_out, A3);
  not not_87 (not_87_out, A2);
  not not_88 (not_88_out, A3);
  not not_89 (not_89_out, A0);
  not not_90 (not_90_out, A4);
  not not_91 (not_91_out, A1);
  not not_92 (not_92_out, A1);
  not not_93 (not_93_out, A4);
  not not_94 (not_94_out, A2);
  not not_95 (not_95_out, A0);
  and and_1 (and_1_out, not_1_out, not_2_out, not_3_out);
  and and_2 (and_2_out, not_4_out, A1);
  and and_3 (and_3_out, not_5_out, A2, A0);
  and and_4 (and_4_out, A3, not_6_out, A0);
  and and_5 (and_5_out, A3, A2, not_7_out);
  and and_6 (and_6_out, A4, not_8_out, not_9_out);
  and and_7 (and_7_out, A4, not_10_out, not_11_out);
  and and_8 (and_8_out, A4, A1);
  and and_9 (and_9_out, not_12_out, not_13_out);
  and and_10 (and_10_out, not_14_out, not_15_out, not_16_out);
  and and_11 (and_11_out, not_17_out, not_18_out, A0);
  and and_12 (and_12_out, not_19_out, not_20_out, A1);
  and and_13 (and_13_out, not_21_out, A1, A0);
  and and_14 (and_14_out, not_22_out, A1, A0);
  and and_15 (and_15_out, not_23_out, A3, not_24_out);
  and and_16 (and_16_out, not_25_out, A3, not_26_out);
  and and_17 (and_17_out, A3, not_27_out, not_28_out);
  and and_18 (and_18_out, A4, A2);
  and and_19 (and_19_out, not_29_out, not_30_out);
  and and_20 (and_20_out, not_31_out, not_32_out);
  and and_21 (and_21_out, not_33_out, A0);
  and and_22 (and_22_out, not_34_out, A0);
  and and_23 (and_23_out, not_35_out, not_36_out, A2);
  and and_24 (and_24_out, A3, A1, not_37_out);
  and and_25 (and_25_out, A4, not_38_out);
  and and_26 (and_26_out, A4, not_39_out);
  and and_27 (and_27_out, not_40_out, not_41_out, not_42_out);
  and and_28 (and_28_out, not_43_out, not_44_out, not_45_out, A1);
  and and_29 (and_29_out, not_46_out, A1, not_47_out);
  and and_30 (and_30_out, not_48_out, A1, not_49_out);
  and and_31 (and_31_out, not_50_out, A2, not_51_out, A0);
  and and_32 (and_32_out, A3, A2, not_52_out, not_53_out);
  and and_33 (and_33_out, not_54_out, A3, A2, A0);
  and and_34 (and_34_out, A4, not_55_out, not_56_out);
  and and_35 (and_35_out, A4, A2, A1);
  and and_36 (and_36_out, A4, A3, not_57_out, not_58_out, A0);
  and and_37 (and_37_out, not_59_out, not_60_out, not_61_out);
  and and_38 (and_38_out, not_62_out, A1, not_63_out);
  and and_39 (and_39_out, not_64_out, A1, not_65_out);
  and and_40 (and_40_out, A3, A2, not_66_out, not_67_out);
  and and_41 (and_41_out, A4, not_68_out, not_69_out);
  and and_42 (and_42_out, A4, A3, A2, A1);
  and and_43 (and_43_out, not_70_out, not_71_out, not_72_out);
  and and_44 (and_44_out, not_73_out, not_74_out, A2, not_75_out);
  and and_45 (and_45_out, not_76_out, not_77_out, A2, not_78_out);
  and and_46 (and_46_out, A3, not_79_out, not_80_out);
  and and_47 (and_47_out, A3, A1, not_81_out);
  and and_48 (and_48_out, not_82_out, A3, A2, A1);
  and and_49 (and_49_out, A4, not_83_out, not_84_out, A1);
  and and_50 (and_50_out, A4, A3, not_85_out);
  and and_51 (and_51_out, not_86_out, not_87_out, A1);
  and and_52 (and_52_out, not_88_out, A1, not_89_out);
  and and_53 (and_53_out, not_90_out, A2, not_91_out);
  and and_54 (and_54_out, A3, not_92_out);
  and and_55 (and_55_out, not_93_out, A3, A2);
  and and_56 (and_56_out, A4, not_94_out, not_95_out);
  and and_57 (and_57_out, A4, A2, A1, A0);
  or or_1 (A, and_1_out, and_2_out, and_3_out, and_4_out, and_5_out, and_6_out, and_7_out, and_8_out);
  or or_2 (B, and_9_out, and_10_out, and_11_out, and_12_out, and_13_out, and_14_out, and_15_out, and_16_out, and_17_out, and_18_out);
  or or_3 (C, and_19_out, and_20_out, and_21_out, and_22_out, and_23_out, and_24_out, and_25_out, and_26_out);
  or or_4 (D, and_27_out, and_28_out, and_29_out, and_30_out, and_31_out, and_32_out, and_33_out, and_34_out, and_35_out, and_36_out);
  or or_5 (E, and_37_out, and_38_out, and_39_out, and_40_out, and_41_out, and_42_out);
  or or_6 (F, and_43_out, and_44_out, and_45_out, and_46_out, and_47_out, and_48_out, and_49_out, and_50_out);
  or or_7 (G, and_51_out, and_52_out, and_53_out, and_54_out, and_55_out, and_56_out, and_57_out);
endmodule

module DECODIFICADORES_decenas (
  input  A4,
  input  A3,
  input  A2,
  input  A1,
  input  A0,
  output A,
  output B,
  output C,
  output D,
  output E,
  output F,
  output G
);

  wire and_1_out, and_2_out, and_3_out, and_4_out, and_5_out, and_6_out, and_7_out, and_8_out, and_9_out,
       and_10_out, and_11_out, and_12_out, and_13_out, and_14_out, and_15_out, and_16_out, and_17_out,
       and_18_out, and_19_out, and_20_out, and_21_out, not_1_out, not_2_out, not_3_out, not_4_out, not_5_out,
       not_6_out, not_7_out, not_8_out, not_9_out, not_10_out, not_11_out, not_12_out, not_13_out,
       not_14_out, not_15_out, not_16_out, not_17_out, not_18_out, not_19_out, not_20_out, not_21_out,
       not_22_out, not_23_out, not_24_out, not_25_out, not_26_out, not_27_out, not_28_out, not_29_out;

  not not_1 (not_1_out, A4);
  not not_2 (not_2_out, A3);
  not not_3 (not_3_out, A4);
  not not_4 (not_4_out, A2);
  not not_5 (not_5_out, A1);
  not not_6 (not_6_out, A3);
  not not_7 (not_7_out, A3);
  not not_8 (not_8_out, A2);
  not not_9 (not_9_out, A4);
  not not_10 (not_10_out, A3);
  not not_11 (not_11_out, A4);
  not not_12 (not_12_out, A2);
  not not_13 (not_13_out, A1);
  not not_14 (not_14_out, A3);
  not not_15 (not_15_out, A4);
  not not_16 (not_16_out, A3);
  not not_17 (not_17_out, A4);
  not not_18 (not_18_out, A2);
  not not_19 (not_19_out, A1);
  not not_20 (not_20_out, A3);
  not not_21 (not_21_out, A2);
  not not_22 (not_22_out, A1);
  not not_23 (not_23_out, A0);
  not not_24 (not_24_out, A4);
  not not_25 (not_25_out, A3);
  not not_26 (not_26_out, A4);
  not not_27 (not_27_out, A2);
  not not_28 (not_28_out, A1);
  and and_1 (and_1_out, A4, A2);
  and and_2 (and_2_out, A4, A3);
  and and_3 (and_3_out, not_1_out, not_2_out);
  and and_4 (and_4_out, not_3_out, not_4_out, not_5_out);
  and and_5 (and_5_out, not_6_out, A2);
  and and_6 (and_6_out, A4, A3);
  not not_29 (not_29_out, A4);
  and and_7 (and_7_out, not_7_out, not_8_out);
  and and_8 (and_8_out, A3, A2, A0);
  and and_9 (and_9_out, A3, A2, A1);
  and and_10 (and_10_out, not_9_out, not_10_out);
  and and_11 (and_11_out, not_11_out, not_12_out, not_13_out);
  and and_12 (and_12_out, not_14_out, A2);
  and and_13 (and_13_out, A4, A3);
  and and_14 (and_14_out, not_15_out, not_16_out);
  and and_15 (and_15_out, not_17_out, not_18_out, not_19_out);
  and and_16 (and_16_out, not_20_out, A2);
  and and_17 (and_17_out, A4, A3, not_21_out);
  and and_18 (and_18_out, A4, A3, not_22_out, not_23_out);
  and and_19 (and_19_out, A4, A3, A1, A0);
  and and_20 (and_20_out, not_24_out, not_25_out);
  and and_21 (and_21_out, not_26_out, not_27_out, not_28_out);
  or or_1 (G, and_1_out, and_2_out);
  or or_2 (A, and_3_out, and_4_out, and_5_out, and_6_out);
  or or_3 (C, not_29_out, and_7_out, and_8_out, and_9_out);
  or or_4 (D, and_10_out, and_11_out, and_12_out, and_13_out);
  or or_5 (E, and_14_out, and_15_out, and_16_out, and_17_out, and_18_out, and_19_out);
  or or_6 (F, and_20_out, and_21_out);

  assign B = 1'b1;
endmodule
